# Fritzing sketch Lego_turbine_controller_v3.3 (saved by Fritzing 0.9.3b)
circuit board: 4.33cm x 5cm
breadboards: 1

parts:
  Arduino_Micro = Arduino Micro (Rev3)
  Battery = screw terminal, 2 pins
  Motor = screw terminal, 2 pins
  LED_1 = screw terminal, 2 pins
  LED_2 = screw terminal, 2 pins
  L293D = IC, DIP package, 16 pins [chip_label=L2930]
  R1 = Resistor [tolerance=±5% resistance=220 package=THT]
  R2 = Resistor [tolerance=±5% resistance=220 package=THT]

nets:
  N1: Arduino_Micro.D9_PWM/A9, R2.Pin_0
  N2: Arduino_Micro.D10_PWM/A10, R1.Pin_1
  N3: Arduino_Micro.GND, Battery.pin2, LED_1.pin2, LED_2.pin2, L293D.pin4, L293D.pin5, L293D.pin12, L293D.pin13
  N4: Arduino_Micro.5V, L293D.pin16
  N5: Arduino_Micro.A1, L293D.pin2
  N6: Arduino_Micro.A0, L293D.pin7
  N7: Arduino_Micro.D13_PWM, L293D.pin1
  N8: Battery.pin1, L293D.pin8
  N9: Motor.pin1, L293D.pin3
  N10: Motor.pin2, L293D.pin6
  N11: LED_1.pin1, R2.Pin_1
  N12: LED_2.pin1, R1.Pin_0

notes:
  Windturbine v.3.3
  house-of-it.eu
